# Fritzing sketch Breadboard (saved by Fritzing 0.9.8b)
breadboards: 1

parts:
  Mod1 = Heltec WiFi LoRa 32 V2 [part_number=HTIT-WB32LA]
  Mod2 = KY-019 5V Relay Module [package="Breakout board"]
  R1 = Resistor [tolerance=±5% resistance=1k package="2512 [SMD]"]
  R2 = Resistor [tolerance=±5% resistance=1k package="2512 [SMD]"]
  R3 = Resistor [tolerance=±5% resistance=1k package="2512 [SMD]"]
  JL012-13-5_1 = JL012-13-5.2 Lever (Limit) Switch SPDT + NO + NC [part_number=JL012-13-5.2]
  JL012-13-5_2 = JL012-13-5.2 Lever (Limit) Switch SPDT + NO + NC [part_number=JL012-13-5.2]

nets:
  N1: Mod1.pin_7, Mod2.S, R1.Pin_0
  N2: Mod1.pin_10, R3.Pin_0, JL012-13-5_2.NO
  N3: Mod1.pin_11, R2.Pin_0, JL012-13-5_1.NO
  N4: Mod1.pin_16, Mod1.pin_17, Mod1.GND, Mod2.+, Mod2.-, R1.Pin_1, R2.Pin_1, R3.Pin_1, JL012-13-5_1.C, JL012-13-5_2.C

custom parts:
  KY-019 5V Relay Module: KY-019 5V Relay module, used to control AC circuits. (Special thanks to vanepp for fixing the PCB holes and other errors)
  JL012-13-5.2 Lever (Limit) Switch SPDT + NO + NC: Micro Switch; Model No.: JL012-13.5-2; Actuator Action: Momentary; Actuator Type: Hinge Lever; Contact Configuration: 1NO, 1NC (SPDT) Temperature -25~65℃；Relative humidity: below 85%; Rate Voltage: 125V AC; Rated Current: 1A.
